# Fritzing sketch Ambient_Light_Level (saved by Fritzing 0.9.2b)
breadboards: 1

parts:
  Part1 = Arduino Uno (Rev3)
  U1 = 74HC595 [package="DIP16 [THT]"]
  R1 = Resistor [tolerance=±5% resistance=560 package="2010 [SMD]"]
  R2 = Resistor [tolerance=±5% resistance=560 package="2010 [SMD]"]
  7_Segment2 = 7 Segment Display
  R3 = Resistor [tolerance=±5% resistance=10k package="0603 [SMD]"]
  R4 = PHOTOCELL [package=photocell]

nets:
  N1: Part1.A0, R3.Pin_1, R4.P$1
  N2: Part1.D2, U1.DS
  N3: Part1.D3_PWM, U1.SH_CP
  N4: Part1.D4, U1.ST_CP
  5V: Part1.5V, U1.MR, U1.VCC, R3.Pin_0
  GND: Part1.GND, U1.GND, U1.OE, R2.Pin_0, R4.P$2
  N5: U1.Q1, 7_Segment2.Segment_F
  N6: U1.Q6, 7_Segment2.Segment_B
  N7: U1.Q7, 7_Segment2.Segment_A#10
  N8: U1.Q0, 7_Segment2.Segment_A#1
  N9: R1.Pin_0, 7_Segment2.Segment_E
  N10: R2.Pin_1, 7_Segment2.common_cathode#8
